// Logisim project parcialreducido.circ as structural Verilog: 1 circuit, main circuit main
module main (
  input  A,
  input  B,
  input  C,
  input  D,
  output a_2,
  output b_2,
  output f,
  output g,
  output e,
  output d_2,
  output c_2
);

  wire and_1_out, and_2_out, and_3_out, and_4_out, and_5_out, and_6_out, and_7_out, and_8_out, and_9_out,
       and_10_out, and_11_out, and_12_out, and_13_out, not_1_out, not_2_out, not_3_out, not_4_out, not_5_out,
       not_6_out, not_7_out, not_8_out, not_9_out, not_10_out, not_11_out, not_12_out, not_13_out,
       not_14_out, not_15_out, not_16_out, not_17_out, not_18_out, not_19_out, or_2_out, or_3_out;

  not not_1 (not_1_out, B);
  and and_1 (and_1_out, not_1_out, not_2_out);
  not not_2 (not_2_out, D);
  and and_2 (and_2_out, B, D);
  not not_3 (not_3_out, B);
  not not_4 (not_4_out, C);
  and and_3 (and_3_out, not_4_out, not_5_out);
  not not_5 (not_5_out, D);
  and and_4 (and_4_out, C, D);
  not not_6 (not_6_out, C);
  or or_1 (c_2, not_6_out, D, B);
  not not_7 (not_7_out, B);
  not not_8 (not_8_out, D);
  or or_2 (or_2_out, not_8_out, C);
  not not_9 (not_9_out, D);
  not not_10 (not_10_out, C);
  not not_11 (not_11_out, D);
  not not_12 (not_12_out, B);
  or or_3 (or_3_out, not_12_out, C);
  and and_5 (and_5_out, B, not_13_out);
  not not_13 (not_13_out, C);
  and and_6 (and_6_out, B, not_14_out);
  not not_14 (not_14_out, D);
  not not_15 (not_15_out, C);
  and and_7 (and_7_out, not_15_out, not_16_out);
  not not_16 (not_16_out, D);
  not not_17 (not_17_out, B);
  and and_8 (and_8_out, not_17_out, C);
  and and_9 (and_9_out, B, not_18_out);
  not not_18 (not_18_out, C);
  and and_10 (and_10_out, B, not_19_out);
  not not_19 (not_19_out, D);
  or or_4 (a_2, A, C, and_1_out, and_2_out);
  or or_5 (b_2, not_3_out, and_3_out, and_4_out);
  and and_11 (and_11_out, not_7_out, or_2_out);
  and and_12 (and_12_out, C, not_9_out);
  and and_13 (and_13_out, B, not_10_out, D);
  and and_14 (e, not_11_out, or_3_out);
  or or_6 (f, A, and_5_out, and_6_out, and_7_out);
  or or_7 (g, A, and_8_out, and_9_out, and_10_out);
  or or_8 (d_2, A, and_11_out, and_12_out, and_13_out);
  _7_Segment_Display u_7_segment_display_1 (.g(g), .f(f), .a(a_2), .b(b_2), .e(e), .d(d_2), .c(c_2));  // open: dp
endmodule
